// Logisim project full adder.circ as structural Verilog: 1 circuit, main circuit main
module main (
  input  A,
  input  B,
  input  C,
  output S,
  output C_2
);

  wire and_1_out, and_2_out, xor_1_out, xor_3_out;

  xor xor_1 (xor_1_out, A, B);
  and and_1 (and_1_out, xor_1_out, C);
  xor xor_2 (S, xor_1_out, C);
  buf and_2 (and_2_out, A);  // AND_Gate
  xor xor_3 (xor_3_out, and_1_out, and_2_out);
endmodule
