// Logisim project half adder.circ as structural Verilog: 1 circuit, main circuit main
module main (
  input  A,
  input  B,
  output S,
  output out_4
);

  xor xor_1 (S, A, B);
  and and_1 (out_4, A, B);
endmodule
